# Fritzing sketch hello_world2 (saved by Fritzing 0.9.2b)
breadboards: 1

parts:
  Bauteil1 = Arduino Uno (Rev3)
  R1 = Resistor [tolerance=±5% resistance=220 package=THT]
  LED1 = LED - 5mm [color="Red (633nm)" package="5 mm [THT]"]

nets:
  N1: Bauteil1.D13/SCK, R1.Pin_0
  N2: Bauteil1.GND, LED1.cathode
  N3: R1.Pin_1, LED1.anode

// code stored in the sketch: hello_world.ino
// hello_world.ino
const int pin = 13; // also the SMD Led on the Arduino

void setup()
{
  // Set pin 13 in output mode
  pinMode(pin, OUTPUT);
}

void loop()
{
  digitalWrite(pin, HIGH);  // turn the LED on
  delay(1000);              // wait for a second
  digitalWrite(pin, LOW);   // turn the LED off
  delay(250);               // wait for 250 milli seconds
}
