# Fritzing sketch pwm (saved by Fritzing 0.9.2b)
breadboards: 1

parts:
  Bauteil1 = Arduino Ethernet Shield (Rev3)
  R1 = Resistor [tolerance=±5% resistance=220 package=THT]
  LED1 = LED - 5mm [color="Red (633nm)" package="5 mm [THT]"]  # not connected

nets:
  N1: Bauteil1.PWM_D11, Bauteil1.A0, R1.Pin_1
