# Fritzing sketch ir_receive (saved by Fritzing 0.9.2b)
breadboards: 1

parts:
  Receiver = Arduino Uno (Rev3)
  LED1 = LED - 5mm [color="Infrared (940nm)" package="5 mm [THT]"]
  Q1 = PNP-Transistor [package="TO92 [THT]"]
  Sender = Arduino Uno (Rev3)
  R1 = Resistor [tolerance=±1% resistance=100 package=THT]

nets:
  N1: Receiver.D13/SCK, Q1.C
  N2: Receiver.5V, Q1.E
  N3: Receiver.GND, Q1.B
  N4: LED1.cathode, Sender.GND
  N5: LED1.anode, R1.Pin_0
  N6: Sender.D3_PWM, R1.Pin_1
