# Fritzing sketch sonar (saved by Fritzing 0.9.2b)
breadboards: 1

parts:
  Bauteil1 = Arduino Uno (Rev3)
  T1 = LM35 Temperature Sensor [package="TO92 [THT]"]
  LED1 = RGB LED (com. cathode, rgb) [package="5 mm [THT]"]

nets:
  N1: Bauteil1.A0, T1.Vout
  N2: Bauteil1.D8, LED1.common_cathode
  N3: Bauteil1.D9_PWM, LED1.green_anode
  N4: Bauteil1.5V, T1.+Vs, LED1.red_anode
  GND: Bauteil1.GND, T1.GND, LED1.blue_anode
