# Fritzing sketch pull_down (saved by Fritzing 0.9.2b)
breadboards: 1

parts:
  S1 = Pushbutton [package="[THT]"]
  Bauteil1 = Arduino Uno (Rev3)

nets:
  N1: S1.Pin_1, S1.Pin_2, Bauteil1.D3_PWM
  N2: S1.Pin_3, S1.Pin_4, Bauteil1.5V
