# Fritzing sketch pull_down2 (saved by Fritzing 0.9.2b)
breadboards: 1

parts:
  S1 = Pushbutton [package="[THT]"]
  Bauteil1 = Arduino Uno (Rev3)
  R1 = Resistor [tolerance=±1% resistance=10k package=THT]

nets:
  N1: S1.Pin_1, S1.Pin_2, Bauteil1.D3_PWM, R1.Pin_1
  N2: S1.Pin_3, S1.Pin_4, Bauteil1.5V
  N3: Bauteil1.GND, R1.Pin_0
