# Fritzing sketch potentiometer (saved by Fritzing 0.9.2b)
breadboards: 1

parts:
  R1 = Resistor [tolerance=±5% resistance=220 package=THT]
  R2 = Resistor [tolerance=±5% resistance=220 package=THT]
  R3 = Rotary Potentiometer (Small) [maximum_resistance=100kΩ package=THT]
  LED1 = LED - 5mm [color="Red (633nm)" package="5 mm [THT]"]
  LED2 = LED - 5mm [color="Red (633nm)" package="5 mm [THT]"]
  Bauteil1 = Arduino Uno (Rev3)

nets:
  N1: R1.Pin_0, LED2.cathode
  N2: R1.Pin_1, R2.Pin_1, Bauteil1.5V
  N3: R2.Pin_0, LED1.anode
  N4: R3.leg1, LED2.anode
  N5: R3.wiper, Bauteil1.GND
  N6: R3.leg2, LED1.cathode
