# Fritzing sketch resistors (saved by Fritzing 0.9.2b)
breadboards: 1

parts:
  Bauteil1 = Arduino Uno (Rev3)
  R3 = Resistor [tolerance=±1% resistance=200 package=THT]
  R4 = Resistor [tolerance=±1% resistance=200 package=THT]
  R6 = Resistor [tolerance=±1% resistance=10k package=THT]
  R8 = Resistor [tolerance=±1% resistance=10k package=THT]
  R9 = Resistor [tolerance=±1% resistance=10k package=THT]
  R10 = Resistor [tolerance=±1% resistance=200 package=THT]

nets:
  N1: Bauteil1.A0, R3.Pin_1, R4.Pin_0
  N2: Bauteil1.A1, R9.Pin_1, R10.Pin_0
  N3: Bauteil1.A2, R6.Pin_0, R8.Pin_1
  N4: Bauteil1.5V, R3.Pin_0, R8.Pin_0
  N5: Bauteil1.GND, R4.Pin_1, R6.Pin_1, R10.Pin_1
