# Fritzing sketch resistors_parallel (saved by Fritzing 0.9.2b)
breadboards: 1

parts:
  Bauteil1 = Arduino Uno (Rev3)
  R6 = Resistor [tolerance=±1% resistance=10k package=THT]
  R8 = Resistor [tolerance=±1% resistance=10k package=THT]

nets:
  N1: Bauteil1.5V, R6.Pin_0, R8.Pin_0
  N2: Bauteil1.GND, R6.Pin_1, R8.Pin_1
